# Fritzing sketch open_fridge_door_alarm (saved by Fritzing 0.9.3b)
stripboards: 1

parts:
  U1 = attiny85 [package=dip]
  CR2032_holder = LilyPad Coin Cell Battery Holder
  Freezer = Reed switch [package=THT]
  Fridge = Reed switch [package=THT]
  J1 = Piezo Speaker
  LED1 = LED - 5mm [color="Yellow (592nm)" package="5 mm [THT]"]
  R1 = Resistor [tolerance=±5% resistance=330 package="0805 [SMD]"]

nets:
  N1: U1.Pin_2, R1.Pin_0
  N2: U1.Pin_3, J1.pin2
  GND: U1.Pin_4, CR2032_holder.-, J1.pin1, LED1.cathode
  N3: U1.Pin_5, Freezer.pin_2, Fridge.pin_2
  N4: U1.Pin_6, Fridge.pin_1
  N5: U1.Pin_7, Freezer.pin_1
  N6: U1.Pin_8, CR2032_holder.+
  N7: LED1.anode, R1.Pin_1
